# Fritzing sketch robot (saved by Fritzing 0.9.2b)

parts:
  L1 = Solenoid
  L2 = Solenoid
  L3 = Solenoid
  L4 = Solenoid
  Part1 = Arduino Pro Mini v13
  Q1 = NPN-Transistor [package="TO92 [THT]"]
  R1 = Photocell (LDR) [package=THT]
  LED1 = LED - 5mm [color="Red (633nm)" package="5 mm [THT]"]
  R2 = Resistor [tolerance=±5% resistance=220 package=THT]
  R3 = Resistor [tolerance=±5% resistance=10k package=THT]
  VCC1 = Battery block 9V
  Part2 = Motor Driver 1A Dual TB6612FNG
  Drive = DC Motor
  Steer = DC Motor

nets:
  N1: L1.pin1, L2.pin1, L3.pin1, L4.pin1, Part1.RAW, VCC1.+
  N2: L1.pin2, L2.pin2, L3.pin2, L4.pin2, Q1.C
  VCC: Part1.VCC, LED1.anode, R3.Pin_1, Part2.VCC, Part2.VM
  GND: Part1.GND, Q1.E, R1.pin_1, R2.Pin_1, VCC1.-, Part2.GND
  N3: Part1.D10_PWM/SS, Q1.B
  N4: Part1.D9_PWM, Part2.STBY
  N5: Part1.D8, Part2.BIN2
  N6: Part1.D7, Part2.BIN1
  N7: Part1.D6_PWM, Part2.PWMB
  N8: Part1.D5_PWM, Part2.PWMA
  N9: Part1.D4, Part2.AIN2
  N10: Part1.D3_PWM, R1.pin_0, R3.Pin_0
  N11: Part1.D2, Part2.AIN1
  N12: LED1.cathode, R2.Pin_0
  N13: Part2.B01, Steer.pin_1
  N14: Part2.B02, Steer.pin_2
  N15: Part2.A02, Drive.pin_2
  N16: Part2.A01, Drive.pin_1

// code stored in the sketch: SOEV.ino
//<define the IO pins for easier Refrencce>
// #define is good for IO pins because #define and IO pins are both hard wiring
#define brkpin 10
#define tachpin 3
//</define the IO pins for easier Refrencce>

//<Init Motor Drivers>
// Creadit where cedit is due - This was copied and pasted from the Sparkfun Hookup Guide
//https://github.com/sparkfun/SparkFun_TB6612FNG_Arduino_Library/blob/master/examples/MotorTestRun/MotorTestRun.ino

// This is the library for the TB6612 that contains the class Motor and all the
// functions
#include <SparkFun_TB6612.h>

// Pins for all inputs, keep in mind the PWM defines must be on PWM pins
// the default pins listed are the ones used on the Redbot (ROB-12097) with
// the exception of STBY which the Redbot controls with a physical switch
#define AIN1 2
#define BIN1 7
#define AIN2 4
#define BIN2 8
#define PWMA 5
#define PWMB 6
#define STBY 9

// these constants are used to allow you to make your motor configuration
// line up with function names like forward.  Value can be 1 or -1
const int offsetA = 1;
const int offsetB = 1;

// Initializing motors.  The library will allow you to initialize as many
// motors as you have memory for.  If you are using functions like forward
// that take 2 motors as arguements you can either write new functions or
// call the function more than once.
Motor prop = Motor(AIN1, AIN2, PWMA, offsetA, STBY);
Motor turn = Motor(BIN1, BIN2, PWMB, offsetB, STBY);
//</Init Motor Drivers>

//<Init Variables>
//Floats are evil due to slow computation speeds. AVOID!
unsigned long trk; //use cm
unsigned long loc; //use cm
const unsigned long decel; //use cm*(cm/ms)
unsigned long spd; //speed in cm/ms
//<used by tachometer>
//global becuase they are used in tachLog() and tachCount()
unsigned long lastTach;
unsigned long thisTach;
//<used by tachCount Function>
//</Init Variables>

void setup() {
  //<turn on LED 13 to signify init>
  pinMode(13, OUTPUT);
  digitalWrite(13, HIGH);
  //</turn on LED 13 to signify init>
  //<pin Modes>
  pinMode(brkpin, OUTPUT);
  pinMode(tachpin, INPUT);
  //</pin Modes>
  attachInterrupt(0, tachLog, RISING); //if the tachpin is pulled high (the light shines through the holes in the wheels)
  //Interrupt is used becuase the code may miss it if it is only called during loop
  prop.drive(255); //turn the motor on
  Serial.println("trk,loc,spd,lastTach,thisTach"); //tells the order of the variables when printed
}

void loop() {
  //<log all the variables for debuging>
  Serial.print(trk);
  Serial.print(",");
  Serial.print(loc);
  Serial.print(",");
  Serial.print(spd);
  Serial.print(",");
  Serial.print(lastTach);
  Serial.print(",");
  Serial.println(thisTach);
  //</log all the variable for debugging>
  tachCount();// do the tach maths
  if (trk - loc <= decel * spd) { //if we are running out of track
    prop.brake(); //brake the motors
    digitalWrite(brkpin, HIGH); //fire the solenoids
  }
}

void tachLog() {//interrupt for tachometer
  lastTach = thisTach;//move thisTach into lastTach to make room for the new reading
  thisTach = millis();// get the new reading
}

void tachCount() {
  //<local variables>
  //I use local variables so that if tachcount is called in the middle of the function it wont make the maths go poof.
  unsigned long lclLast = lastTach;
  unsigned long lclThis = thisTach;
  //</local Variables>
  spd = 1822 / (lclThis - lclLast) * 100; //cm/ms, //1.82212373908208 = dist, //* 100 is to avoid floating point stuff
  if (!(lclThis == thisTach) {//if tachLog has been called since we started
  tachCount();//do this function again
    //I love recursion
  }
}
